# Fritzing sketch RC_Arducar (saved by Fritzing 0.9.2b)
breadboards: 1

parts:
  Parte1 = Adafruit Motor/Stepper/Servo Shield [part_number="Adafruit #1438"]
  Parte2 = Bluetooth HC-06
  Parte3 = Arduino Uno (Rev3)
  J1 = Piezo Speaker
  Parte4 = SRF05 Ultrasonic Rangefinder
  M1 = DC Motor
  M2 = DC Motor
  VCC1 = 4 x AAA Battery Mount

nets:
  N1: Parte1.M2A, M2.pin_1
  N2: Parte1.M2B, M2.pin_2
  N3: Parte1.M1B, M1.pin_1
  N4: Parte1.M1A, M1.pin_2
  N5: Parte1.GND, VCC1.-
  N6: Parte1.VMOTOR, VCC1.+
  N7: Parte2.RXD, Parte3.D1/TX
  N8: Parte2.TXD, Parte3.D0/RX
  GND: Parte2.GND, Parte3.GND, J1.pin1, Parte4.GND
  VCC: Parte2.VCC, Parte3.5V, Parte4.VCC
  N9: Parte3.D12/MISO, J1.pin2
  N10: Parte3.D6_PWM, Parte4.Echo
  N11: Parte3.D7, Parte4.Trig

custom parts:
  Adafruit Motor/Stepper/Servo Shield: The original Adafruit Motorshield kit is one of our most beloved kits, which is why we decided to make something even better. We have upgraded the shield kit to make the bestest, easiest way to drive DC and Stepper motors. This shield will make quick work of your next robotics project! We kept the ability to drive up to 4 DC motors or 2 stepper motors, but added many improvements: Instead of a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
